// Logisim project PipelineARM-CPU1.circ as structural Verilog: 1 circuit, main circuit Datapath
module Datapath (
  input  Reset,
  input  Clear_Instr_Mem,
  input  Clear_Data_Mem
);

  wire ALU_zero, branchcontrol_1_control, Clock_out, Ctrl_alusrc, Ctrl_conditional_branch, Ctrl_memread,
       Ctrl_memtoreg, Ctrl_memwrite, Ctrl_reg2loc, Ctrl_regwrite, Ctrl_unconditional_branch,
       pipereg2ctrl_1_alusrc_out, pipereg2ctrl_1_cond_branch_out, pipereg2ctrl_1_memread_out,
       pipereg2ctrl_1_memtoreg_out, pipereg2ctrl_1_memwrite_2, pipereg2ctrl_1_regwrite_out,
       pipereg2ctrl_1_uncond_branch_out, pipereg3ctrl_1_cond_branch_out, pipereg3ctrl_1_memread_out,
       pipereg3ctrl_1_memtoreg_out, pipereg3ctrl_1_memwrite_2, pipereg3ctrl_1_regwrite_out,
       pipereg3ctrl_1_uncond_branch_out, pipereg3dp_1_zero_2, pipereg4regctrl_1_memtoreg_out,
       pipereg4regctrl_1_regwrite_out;
  wire [1:0] data_mem_interface_1_mem_control;
  wire [3:0] ALU_Ct_operation, pipereg2aluctrrt_1_alu_ctrl_out;
  wire [4:0] instructiondecode_1_rd_rt, instructiondecode_1_rm, instructiondecode_1_rn, multiplexer_1_out,
       pipereg2aluctrrt_1_rt_out, pipereg3rt_1_rt_out, pipereg4rt_1_rt_out;
  wire [7:0] data_mem_interface_1_address_to_mem, inst_mem_interface_1_to_inst_mem;
  wire [10:0] instructiondecode_1_opcode, instructiondecode_1_opcodealu;
  wire [31:0] adder_1_out, ALU_result, branchaddress_1_branchaddress, data_mem_interface_1_data_from_mem,
       data_mem_interface_1_data_from_memory, inst_mem_interface_1_instruction,
       instructiondecode_1_sign_ext_0_31, multiplexer_2_out, multiplexer_3_out, multiplexer_4_out, PC_q,
       pipereg1_1_ir_out, pipereg1_1_pc_out, pipereg2dp_1_a_reg, pipereg2dp_1_b_reg, pipereg2dp_1_sign_ext_2,
       pipereg2pc_1_pc_out, pipereg3baddress_1_nextaddress_out, pipereg3dp_1_b_reg_2, pipereg3dp_1_result_2,
       pipereg4dp_1_alu_result_out, pipereg4dp_1_data_from_memory_out, ram_1_data, Register_file_readdata1,
       Register_file_readdata2, signextend_1_out_2;

  Register #(.width(32)) PC (.D(multiplexer_3_out), .Q(PC_q), .clk(Clock_out), .clr(Reset));  // open: en
  Clock Clock (.out(Clock_out));
  Adder #(.width(32)) adder_1 (.a(32'h4), .b(PC_q), .out(adder_1_out));  // open: cin, cout
  Inst_Mem_Interface inst_mem_interface_1 (
    .Instruction_Address(PC_q), .To_Inst_Mem(inst_mem_interface_1_to_inst_mem),
    .Mem_To_Interface(ram_1_data), .Instruction(inst_mem_interface_1_instruction));
  PipeReg1 pipereg1_1 (
    .PC(PC_q), .Instruction(inst_mem_interface_1_instruction), .Clock(Clock_out), .Reset(Reset),
    .PC_out(pipereg1_1_pc_out), .IR_out(pipereg1_1_ir_out));
  InstructionDecode instructiondecode_1 (
    .Instruction(pipereg1_1_ir_out), .opcode(instructiondecode_1_opcode), .rn(instructiondecode_1_rn),
    .rm(instructiondecode_1_rm), .rd_rt(instructiondecode_1_rd_rt),
    .Sign_Ext_0_31(instructiondecode_1_sign_ext_0_31), .opcodeALU(instructiondecode_1_opcodealu));  // open: shamt
  RAM #(.dataWidth(32)) ram_1 (
    .addr(inst_mem_interface_1_to_inst_mem), .data(ram_1_data), .sel(1'b1), .clk(1'b0), .ld(1'b1),
    .clr(Clear_Instr_Mem));
  Control Ctrl (
    .op(instructiondecode_1_opcode), .Unconditional_Branch(Ctrl_unconditional_branch),
    .Conditional_Branch(Ctrl_conditional_branch), .MemToReg(Ctrl_memtoreg), .MemRead(Ctrl_memread),
    .MemWrite(Ctrl_memwrite), .ALUsrc(Ctrl_alusrc), .RegWrite(Ctrl_regwrite), .Reg2Loc(Ctrl_reg2loc));
  Registers Register_file (
    .ReadRegister1(instructiondecode_1_rn), .ReadRegister2(multiplexer_1_out),
    .WriteRegister(pipereg4rt_1_rt_out), .WriteData(multiplexer_4_out),
    .Write(pipereg4regctrl_1_regwrite_out), .Clock(Clock_out), .Clear(Reset),
    .ReadData1(Register_file_readdata1), .ReadData2(Register_file_readdata2));
  Multiplexer #(.width(5), .enable("false")) multiplexer_1 (
    .in0(instructiondecode_1_rm), .in1(instructiondecode_1_rd_rt), .out(multiplexer_1_out), .sel(Ctrl_reg2loc));
  SignExtend signextend_1 (._0_31(instructiondecode_1_sign_ext_0_31), .out_2(signextend_1_out_2));
  ALUcontrol ALU_Ct (.opcode(instructiondecode_1_opcodealu), .Operation(ALU_Ct_operation));
  PipeReg2PC pipereg2pc_1 (.PC_in(pipereg1_1_pc_out), .Clock(Clock_out), .Reset(Reset), .PC_out(pipereg2pc_1_pc_out));
  PipeReg2Ctrl pipereg2ctrl_1 (
    .Unconditional_Branch(Ctrl_unconditional_branch), .Conditional_Branch(Ctrl_conditional_branch),
    .MemToReg(Ctrl_memtoreg), .MemRead(Ctrl_memread), .MemWrite(Ctrl_memwrite), .ALUsrc(Ctrl_alusrc),
    .RegWrite(Ctrl_regwrite), .Clock(Clock_out), .Reset(Reset),
    .Uncond_Branch_out(pipereg2ctrl_1_uncond_branch_out), .Cond_Branch_out(pipereg2ctrl_1_cond_branch_out),
    .MemToReg_out(pipereg2ctrl_1_memtoreg_out), .MemRead_out(pipereg2ctrl_1_memread_out),
    .MemWrite_2(pipereg2ctrl_1_memwrite_2), .ALUsrc_out(pipereg2ctrl_1_alusrc_out),
    .RegWrite_out(pipereg2ctrl_1_regwrite_out));
  PipeReg2DP pipereg2dp_1 (
    .A_Register(Register_file_readdata1), .B_Register(Register_file_readdata2),
    .Sign_Ext(signextend_1_out_2), .Clock(Clock_out), .Reset(Reset), .A_Reg(pipereg2dp_1_a_reg),
    .B_Reg(pipereg2dp_1_b_reg), .Sign_Ext_2(pipereg2dp_1_sign_ext_2));
  PipeReg2ALUCtrRt pipereg2aluctrrt_1 (
    .ALU_ctrl(ALU_Ct_operation), .Rt(instructiondecode_1_rd_rt), .Clock(Clock_out), .Reset(Reset),
    .ALU_ctrl_out(pipereg2aluctrrt_1_alu_ctrl_out), .Rt_out(pipereg2aluctrrt_1_rt_out));
  BranchAddress branchaddress_1 (
    .PC(pipereg2pc_1_pc_out), .Address(pipereg2dp_1_sign_ext_2), .BranchAddress(branchaddress_1_branchaddress));
  ALU ALU (
    .A(pipereg2dp_1_a_reg), .B(multiplexer_2_out), .Operation(pipereg2aluctrrt_1_alu_ctrl_out),
    .Zero(ALU_zero), .Result(ALU_result));  // open: Sign, Overflow, Carry_Out
  Multiplexer #(.width(32), .enable("false")) multiplexer_2 (
    .in0(pipereg2dp_1_b_reg), .in1(pipereg2dp_1_sign_ext_2), .out(multiplexer_2_out),
    .sel(pipereg2ctrl_1_alusrc_out));
  PipeReg3BAddress pipereg3baddress_1 (
    .Address_in(branchaddress_1_branchaddress), .Clock(Clock_out), .Reset(Reset),
    .NextAddress_out(pipereg3baddress_1_nextaddress_out));
  PipeReg3Ctrl pipereg3ctrl_1 (
    .Unconditional_Branch(pipereg2ctrl_1_uncond_branch_out),
    .Conditional_Branch(pipereg2ctrl_1_cond_branch_out), .MemToReg(pipereg2ctrl_1_memtoreg_out),
    .MemRead(pipereg2ctrl_1_memread_out), .MemWrite(pipereg2ctrl_1_memwrite_2),
    .RegWrite(pipereg2ctrl_1_regwrite_out), .Clock(Clock_out), .Reset(Reset),
    .Uncond_Branch_out(pipereg3ctrl_1_uncond_branch_out), .Cond_Branch_out(pipereg3ctrl_1_cond_branch_out),
    .MemToReg_out(pipereg3ctrl_1_memtoreg_out), .MemRead_out(pipereg3ctrl_1_memread_out),
    .MemWrite_2(pipereg3ctrl_1_memwrite_2), .RegWrite_out(pipereg3ctrl_1_regwrite_out));
  PipeReg3DP pipereg3dp_1 (
    .Zero(ALU_zero), .Result(ALU_result), .B_reg(pipereg2dp_1_b_reg), .Clock(Clock_out), .Reset(Reset),
    .Zero_2(pipereg3dp_1_zero_2), .Result_2(pipereg3dp_1_result_2), .B_reg_2(pipereg3dp_1_b_reg_2));
  PipeReg3Rt pipereg3rt_1 (
    .Rt_in(pipereg2aluctrrt_1_rt_out), .Clock(Clock_out), .Reset(Reset), .Rt_out(pipereg3rt_1_rt_out));
  BranchControl branchcontrol_1 (
    .UnconditionalBranch(pipereg3ctrl_1_uncond_branch_out),
    .ConditionalBranchCBZ(pipereg3ctrl_1_cond_branch_out), .Zero(pipereg3dp_1_zero_2),
    .control(branchcontrol_1_control));
  Multiplexer #(.width(32), .enable("false")) multiplexer_3 (
    .in0(adder_1_out), .in1(pipereg3baddress_1_nextaddress_out), .out(multiplexer_3_out),
    .sel(branchcontrol_1_control));
  PipeReg4RegCtrl pipereg4regctrl_1 (
    .MemToReg_In(pipereg3ctrl_1_memtoreg_out), .RegWrite_In(pipereg3ctrl_1_regwrite_out), .Clock(Clock_out),
    .Reset(Reset), .MemToReg_Out(pipereg4regctrl_1_memtoreg_out),
    .RegWrite_Out(pipereg4regctrl_1_regwrite_out));
  PipeReg4DP pipereg4dp_1 (
    .ALU_Result_In(pipereg3dp_1_result_2), .Data_From_Memory_In(data_mem_interface_1_data_from_memory),
    .Clock(Clock_out), .Reset(Reset), .ALU_Result_Out(pipereg4dp_1_alu_result_out),
    .Data_From_Memory_Out(pipereg4dp_1_data_from_memory_out));
  Data_Mem_Interface data_mem_interface_1 (
    .Data_Address(pipereg3dp_1_result_2), .Data_to_Memory(pipereg3dp_1_b_reg_2),
    .MemWrite(pipereg3ctrl_1_memwrite_2), .MemRead(pipereg3ctrl_1_memread_out),
    .Clock___Rising_Edge(Clock_out), .Address_To_Mem(data_mem_interface_1_address_to_mem),
    .Mem_Control(data_mem_interface_1_mem_control), .Data_To_Mem(data_mem_interface_1_data_from_mem),
    .Data_From_Mem(data_mem_interface_1_data_from_mem),
    .Data_from_Memory(data_mem_interface_1_data_from_memory));
  PipeReg4Rt pipereg4rt_1 (.Rt_in(pipereg3rt_1_rt_out), .Clock(Clock_out), .Reset(Reset), .Rt_out(pipereg4rt_1_rt_out));
  RAM #(.dataWidth(32)) ram_2 (
    .addr(data_mem_interface_1_address_to_mem), .data(data_mem_interface_1_data_from_mem), .sel(1'b1),
    .clk(data_mem_interface_1_mem_control[0]), .ld(data_mem_interface_1_mem_control[1]), .clr(Clear_Data_Mem));
  Multiplexer #(.width(32), .enable("false")) multiplexer_4 (
    .in0(pipereg4dp_1_alu_result_out), .in1(pipereg4dp_1_data_from_memory_out), .out(multiplexer_4_out),
    .sel(pipereg4regctrl_1_memtoreg_out));

  // Notes on the sheet:
  //   F19
  //   Tuan Wang
  //   11/6/19
  //   Decode
  //   Extend
  //   EX/Mem
  //   Mem/WB
endmodule
