// Logisim project control.circ as structural Verilog: 6 circuits, main circuit ALUcontrol_0
module ALUcontrol_0 (
  input  op_21,
  input  op_22,
  input  op_23,
  input  op_24,
  input  op_25,
  input  op_26,
  input  op_27,
  input  op_28,
  input  op_29,
  input  op_30,
  input  op_31,
  output Operation_3,
  output Operation_2,
  output Operation_1,
  output Operation_0
);

  wire and_1_out, and_2_out, not_1_out, or_1_out;

  and and_1 (and_1_out, op_27, op_28, op_29, op_30, op_31);
  and and_2 (and_2_out, op_24, op_31);
  or or_1 (or_1_out, op_26, op_29);
  and and_3 (Operation_2, op_30, and_2_out);
  or or_2 (Operation_1, and_2_out, op_28);
  and and_4 (Operation_0, or_1_out, not_1_out);
  not not_1 (not_1_out, and_1_out);

  assign Operation_3 = 1'b0;
endmodule

module Control_0 (
  input  op_21,
  input  op_22,
  input  op_23,
  input  op_24,
  input  op_25,
  input  op_26,
  input  op_27,
  input  op_28,
  input  op_29,
  input  op_30,
  input  op_31,
  output Unconditional_Branch,
  output Conditional_Branch,
  output MemToReg,
  output MemRead,
  output MemWrite,
  output ALUsrc,
  output RegWrite,
  output Reg2Loc
);

  wire and_2_out, and_4_out, and_5_out, not_1_out, not_2_out;

  and and_1 (Conditional_Branch, op_31, op_29, op_26);
  and and_2 (and_2_out, op_26, op_28);
  and and_3 (ALUsrc, op_31, op_27, op_28, op_29, op_30);
  not not_1 (not_1_out, Unconditional_Branch);
  and and_4 (and_4_out, not_1_out, not_2_out, op_25);
  xor xor_1 (Unconditional_Branch, and_2_out, Conditional_Branch);
  not not_2 (not_2_out, Conditional_Branch);
  and and_5 (and_5_out, op_22, not_1_out, not_2_out);
  or or_1 (RegWrite, and_4_out, and_5_out);
  and and_6 (MemRead, and_5_out, ALUsrc);
  or or_2 (Reg2Loc, MemWrite, op_26);
  xor xor_2 (MemWrite, MemRead, ALUsrc);

  assign MemToReg = ALUsrc;
endmodule

module Fake_Control (
  input  [7:0] Test,
  input  [10:0] op,
  output Unconditional_Branch,
  output Conditional_Branch,
  output MemToReg,
  output MemRead,
  output MemWrite,
  output ALUsrc,
  output RegWrite,
  output Reg2Loc
);


  assign ALUsrc = Test[5];
  assign Conditional_Branch = Test[1];
  assign MemRead = Test[3];
  assign MemToReg = Test[2];
  assign MemWrite = Test[4];
  assign Reg2Loc = Test[7];
  assign RegWrite = Test[6];
  assign Unconditional_Branch = Test[0];
endmodule

module Fake_ALUcontrol (
  input  [3:0] test,
  input  [10:0] opcode,
  output [3:0] Operation
);


  assign Operation = test;
endmodule

module Control (
  input  [10:0] op,
  output Unconditional_Branch,
  output Conditional_Branch,
  output MemToReg,
  output MemRead,
  output MemWrite,
  output ALUsrc,
  output RegWrite,
  output Reg2Loc
);

  Control_0 control_0_1 (
    .op_21(op[0]), .op_22(op[1]), .op_23(op[2]), .op_24(op[3]), .op_25(op[4]), .op_26(op[5]), .op_27(op[6]),
    .op_28(op[7]), .op_29(op[8]), .op_30(op[9]), .op_31(op[10]), .Unconditional_Branch(Unconditional_Branch),
    .Conditional_Branch(Conditional_Branch), .MemToReg(MemToReg), .MemRead(MemRead), .MemWrite(MemWrite),
    .ALUsrc(ALUsrc), .RegWrite(RegWrite), .Reg2Loc(Reg2Loc));

  // Notes on the sheet:
  //   S19
endmodule

module ALUcontrol (
  input  [10:0] opcode,
  output [3:0] Operation
);

  ALUcontrol_0 alucontrol_0_1 (
    .op_21(opcode[0]), .op_22(opcode[1]), .op_23(opcode[2]), .op_24(opcode[3]), .op_25(opcode[4]),
    .op_26(opcode[5]), .op_27(opcode[6]), .op_28(opcode[7]), .op_29(opcode[8]), .op_30(opcode[9]),
    .op_31(opcode[10]), .Operation_3(Operation[3]), .Operation_2(Operation[2]), .Operation_1(Operation[1]),
    .Operation_0(Operation[0]));

  // Notes on the sheet:
  //   S19
endmodule
