// Logisim project pipelineRegisters.circ as structural Verilog: 12 circuits, main circuit PipeReg2PC
module PipeReg1 (
  input  [31:0] PC,
  input  [31:0] Instruction,
  input  Clock,
  input  Reset,
  output [31:0] PC_out,
  output [31:0] IR_out
);

  Register #(.width(32)) PC_Reg (.D(PC), .Q(PC_out), .clk(Clock), .clr(Reset));  // open: en
  Register #(.width(32)) IR (.D(Instruction), .Q(IR_out), .clk(Clock), .clr(Reset));  // open: en

  // Notes on the sheet:
  //   S19
endmodule

module PipeReg2PC (
  input  [31:0] PC_in,
  input  Clock,
  input  Reset,
  output [31:0] PC_out
);

  Register #(.width(32)) PC_reg (.D(PC_in), .Q(PC_out), .clk(Clock), .clr(Reset));  // open: en
endmodule

module PipeReg2DP (
  input  [31:0] A_Register,
  input  [31:0] B_Register,
  input  [31:0] Sign_Ext,
  input  Clock,
  input  Reset,
  output [31:0] A_Reg,
  output [31:0] B_Reg,
  output [31:0] Sign_Ext_2
);

  Register #(.width(32)) u_A_reg (.D(A_Register), .Q(A_Reg), .clk(Clock), .clr(Reset));  // open: en
  Register #(.width(32)) u_B_Reg (.D(B_Register), .Q(B_Reg), .clk(Clock), .clr(Reset));  // open: en
  Register #(.width(32)) Immediate_sign_extended (.D(Sign_Ext), .Q(Sign_Ext_2), .clk(Clock), .clr(Reset));  // open: en
endmodule

module PipeReg2ALUCtrRt (
  input  [3:0] ALU_ctrl,
  input  [4:0] Rt,
  input  Clock,
  input  Reset,
  output [3:0] ALU_ctrl_out,
  output [4:0] Rt_out
);

  Register #(.width(4)) ALU_Control (.D(ALU_ctrl), .Q(ALU_ctrl_out), .clk(Clock), .clr(Reset));  // open: en
  Register #(.width(5)) u_Rt (.D(Rt), .Q(Rt_out), .clk(Clock), .clr(Reset));  // open: en
endmodule

module PipeReg2Ctrl (
  input  Unconditional_Branch,
  input  Conditional_Branch,
  input  MemToReg,
  input  MemRead,
  input  MemWrite,
  input  ALUsrc,
  input  RegWrite,
  input  Clock,
  input  Reset,
  output Uncond_Branch_out,
  output Cond_Branch_out,
  output MemToReg_out,
  output MemRead_out,
  output MemWrite_2,
  output ALUsrc_out,
  output RegWrite_out
);

  Register #(.width(7)) PipelineReg2c (
    .D({RegWrite, ALUsrc, MemWrite, MemRead, MemToReg, Conditional_Branch, Unconditional_Branch}),
    .Q({RegWrite_out, ALUsrc_out, MemWrite_2, MemRead_out, MemToReg_out, Cond_Branch_out, Uncond_Branch_out}),
    .clk(Clock), .clr(Reset));  // open: en
endmodule

module PipeReg3DP (
  input  Zero,
  input  [31:0] Result,
  input  [31:0] B_reg,
  input  Clock,
  input  Reset,
  output Zero_2,
  output [31:0] Result_2,
  output [31:0] B_reg_2
);

  Register #(.width(1)) u_Zero (.D(Zero), .Q(Zero_2), .clk(Clock), .clr(Reset));  // open: en
  Register #(.width(32)) u_Result (.D(Result), .Q(Result_2), .clk(Clock), .clr(Reset));  // open: en
  Register #(.width(32)) u_B_reg (.D(B_reg), .Q(B_reg_2), .clk(Clock), .clr(Reset));  // open: en
endmodule

module PipeReg3Rt (
  input  [4:0] Rt_in,
  input  Clock,
  input  Reset,
  output [4:0] Rt_out
);

  Register #(.width(5)) Rt (.D(Rt_in), .Q(Rt_out), .clk(Clock), .clr(Reset));  // open: en
endmodule

module PipeReg3BAddress (
  input  [31:0] Address_in,
  input  Clock,
  input  Reset,
  output [31:0] NextAddress_out
);

  Register #(.width(32)) Address (.D(Address_in), .Q(NextAddress_out), .clk(Clock), .clr(Reset));  // open: en
endmodule

module PipeReg3Ctrl (
  input  Unconditional_Branch,
  input  Conditional_Branch,
  input  MemToReg,
  input  MemRead,
  input  MemWrite,
  input  RegWrite,
  input  Clock,
  input  Reset,
  output Uncond_Branch_out,
  output Cond_Branch_out,
  output MemToReg_out,
  output MemRead_out,
  output MemWrite_2,
  output RegWrite_out
);

  Register #(.width(6)) PipelineReg3c (
    .D({RegWrite, MemWrite, MemRead, MemToReg, Conditional_Branch, Unconditional_Branch}),
    .Q({RegWrite_out, MemWrite_2, MemRead_out, MemToReg_out, Cond_Branch_out, Uncond_Branch_out}),
    .clk(Clock), .clr(Reset));  // open: en
endmodule

module PipeReg4Rt (
  input  [4:0] Rt_in,
  input  Clock,
  input  Reset,
  output [4:0] Rt_out
);

  Register #(.width(5)) Rt (.D(Rt_in), .Q(Rt_out), .clk(Clock), .clr(Reset));  // open: en
endmodule

module PipeReg4DP (
  input  [31:0] ALU_Result_In,
  input  [31:0] Data_From_Memory_In,
  input  Clock,
  input  Reset,
  output [31:0] ALU_Result_Out,
  output [31:0] Data_From_Memory_Out
);

  Register #(.width(32)) ALU_Result (.D(ALU_Result_In), .Q(ALU_Result_Out), .clk(Clock), .clr(Reset));  // open: en
  Register #(.width(32)) Data_From_Memory (
    .D(Data_From_Memory_In), .Q(Data_From_Memory_Out), .clk(Clock), .clr(Reset));  // open: en
endmodule

module PipeReg4RegCtrl (
  input  MemToReg_In,
  input  RegWrite_In,
  input  Clock,
  input  Reset,
  output MemToReg_Out,
  output RegWrite_Out
);

  Register #(.width(1)) MemToReg (.D(MemToReg_In), .Q(MemToReg_Out), .clk(Clock), .clr(Reset));  // open: en
  Register #(.width(1)) RegWrite (.D(RegWrite_In), .Q(RegWrite_Out), .clk(Clock), .clr(Reset));  // open: en
endmodule
