// Logisim project PipelineARM-CPU1.circ as structural Verilog: 1 circuit, main circuit Datapath
module Datapath (
  input  Reset,
  input  Clear_Instr_Mem,
  input  Clear_Data_Mem
);

  wire ALU_p4, ALU_p5, Clock_out, Ctrl_alusrc, Ctrl_conditional_branch, Ctrl_memread, Ctrl_memtoreg,
       Ctrl_memwrite, Ctrl_reg2loc, Ctrl_regwrite, Ctrl_unconditional_branch, data_mem_interface_1_p1,
       data_mem_interface_1_p2, data_mem_interface_1_p11, data_mem_interface_1_p12, data_mem_interface_1_p18,
       instructiondecode_1_p3, instructiondecode_1_p6, Register_file_p1, Register_file_p2, Register_file_p7,
       Register_file_p14, Register_file_p15, Register_file_p16, Register_file_p17, Register_file_p18,
       Register_file_p19, Register_file_p20;
  wire [1:0] data_mem_interface_1_p7;
  wire [3:0] ALU_Ct_operation, pipereg2aluctrrt_1_alu_ctrl_out;
  wire [4:0] instructiondecode_1_p4, instructiondecode_1_p5, Register_file_p4, signextend_1_p3;
  wire [7:0] data_mem_interface_1_p6, inst_mem_interface_1_p2;
  wire [10:0] instructiondecode_1_p2, instructiondecode_1_p7;
  wire [31:0] adder_1_out, ALU_p2, data_mem_interface_1_p8, data_mem_interface_1_p9,
       data_mem_interface_1_p16, data_mem_interface_1_p17, data_mem_interface_1_p19, inst_mem_interface_1_p3,
       inst_mem_interface_1_p4, multiplexer_3_out, PC_q, pipereg1_1_ir_out, pipereg1_1_pc_out,
       pipereg2dp_1_a_reg, pipereg2dp_1_b_reg, pipereg2dp_1_sign_ext_2, Register_file_p11, Register_file_p12,
       Register_file_p13, signextend_1_p2;

  Register #(.width(32)) PC (.D(multiplexer_3_out), .Q(PC_q), .clk(Clock_out), .clr(Reset));  // open: en
  Clock Clock (.out(Clock_out));
  Adder #(.width(32)) adder_1 (.a(32'h4), .b(PC_q), .out(adder_1_out));  // open: cin, cout
  // Inst_Mem_Interface inst_mem_interface_1: pin names not known; wires that end beside it: PC_q, inst_mem_interface_1_p2, inst_mem_interface_1_p3, inst_mem_interface_1_p4
  PipeReg1 pipereg1_1 (
    .PC(PC_q), .Instruction(inst_mem_interface_1_p4), .Clock(Clock_out), .Reset(Reset),
    .PC_out(pipereg1_1_pc_out), .IR_out(pipereg1_1_ir_out));
  // InstructionDecode instructiondecode_1: pin names not known; wires that end beside it: pipereg1_1_ir_out, instructiondecode_1_p2, instructiondecode_1_p3, instructiondecode_1_p4, instructiondecode_1_p5, instructiondecode_1_p6, instructiondecode_1_p7
  RAM #(.dataWidth(32)) ram_1 (
    .addr(inst_mem_interface_1_p2), .data(inst_mem_interface_1_p3), .sel(1'b1), .clk(1'b0), .ld(1'b1),
    .clr(Clear_Instr_Mem));
  Control Ctrl (
    .op(instructiondecode_1_p2), .Unconditional_Branch(Ctrl_unconditional_branch),
    .Conditional_Branch(Ctrl_conditional_branch), .MemToReg(Ctrl_memtoreg), .MemRead(Ctrl_memread),
    .MemWrite(Ctrl_memwrite), .ALUsrc(Ctrl_alusrc), .RegWrite(Ctrl_regwrite), .Reg2Loc(Ctrl_reg2loc));
  // Registers Register_file: pin names not known; wires that end beside it: Register_file_p1, Register_file_p2, instructiondecode_1_p3, Register_file_p4, Register_file_p1, Register_file_p2, Register_file_p7, Register_file_p7, Clock_out, Reset, Register_file_p11, Register_file_p12, Register_file_p13, Register_file_p14, Register_file_p15, Register_file_p16, Register_file_p17, Register_file_p18, Register_file_p19, Register_file_p20
  Multiplexer #(.width(5), .enable("false")) multiplexer_1 (
    .in0(instructiondecode_1_p4), .in1(instructiondecode_1_p5), .out(Register_file_p4), .sel(Ctrl_reg2loc));
  // SignExtend signextend_1: pin names not known; wires that end beside it: instructiondecode_1_p6, signextend_1_p2, signextend_1_p3
  ALUcontrol ALU_Ct (.opcode(instructiondecode_1_p7), .Operation(ALU_Ct_operation));
  PipeReg2PC pipereg2pc_1 (.PC_in(pipereg1_1_pc_out), .Clock(Clock_out), .Reset(Reset), .PC_out(Register_file_p13));
  PipeReg2Ctrl pipereg2ctrl_1 (
    .Unconditional_Branch(Ctrl_unconditional_branch), .Conditional_Branch(Ctrl_conditional_branch),
    .MemToReg(Ctrl_memtoreg), .MemRead(Ctrl_memread), .MemWrite(Ctrl_memwrite), .ALUsrc(Ctrl_alusrc),
    .RegWrite(Ctrl_regwrite), .Clock(Clock_out), .Reset(Reset), .Uncond_Branch_out(Register_file_p14),
    .Cond_Branch_out(Register_file_p15), .MemToReg_out(Register_file_p16), .MemRead_out(Register_file_p17),
    .MemWrite_2(Register_file_p18), .ALUsrc_out(Register_file_p19), .RegWrite_out(Register_file_p20));
  PipeReg2DP pipereg2dp_1 (
    .A_Register(Register_file_p11), .B_Register(Register_file_p12), .Sign_Ext(signextend_1_p2),
    .Clock(Clock_out), .Reset(Reset), .A_Reg(pipereg2dp_1_a_reg), .B_Reg(pipereg2dp_1_b_reg),
    .Sign_Ext_2(pipereg2dp_1_sign_ext_2));
  PipeReg2ALUCtrRt pipereg2aluctrrt_1 (
    .ALU_ctrl(ALU_Ct_operation), .Rt(instructiondecode_1_p5), .Clock(Clock_out), .Reset(Reset),
    .ALU_ctrl_out(pipereg2aluctrrt_1_alu_ctrl_out), .Rt_out(signextend_1_p3));
  // ALU ALU: pin names not known; wires that end beside it: pipereg2dp_1_a_reg, ALU_p2, pipereg2aluctrrt_1_alu_ctrl_out, ALU_p4, ALU_p5, Clock_out, ALU_p4, ALU_p5, pipereg2dp_1_b_reg, Reset
  Multiplexer #(.width(32), .enable("false")) multiplexer_2 (
    .in0(pipereg2dp_1_b_reg), .in1(pipereg2dp_1_sign_ext_2), .out(ALU_p2));  // open: sel
  Multiplexer #(.width(32), .enable("false")) multiplexer_3 (
    .in0(adder_1_out), .in1(data_mem_interface_1_p9), .out(multiplexer_3_out), .sel(data_mem_interface_1_p12));
  // Data_Mem_Interface data_mem_interface_1: pin names not known; wires that end beside it: data_mem_interface_1_p1, data_mem_interface_1_p2, data_mem_interface_1_p1, data_mem_interface_1_p2, Clock_out, data_mem_interface_1_p6, data_mem_interface_1_p7, data_mem_interface_1_p8, data_mem_interface_1_p9, data_mem_interface_1_p8, data_mem_interface_1_p11, data_mem_interface_1_p12, data_mem_interface_1_p11, Clock_out, Reset, data_mem_interface_1_p16, data_mem_interface_1_p17, data_mem_interface_1_p18, data_mem_interface_1_p19
  RAM #(.dataWidth(32)) ram_2 (
    .addr(data_mem_interface_1_p6), .data(data_mem_interface_1_p8), .sel(1'b1),
    .clk(data_mem_interface_1_p7[0]), .ld(data_mem_interface_1_p7[1]), .clr(Clear_Data_Mem));
  Multiplexer #(.width(32), .enable("false")) multiplexer_4 (
    .in0(data_mem_interface_1_p16), .in1(data_mem_interface_1_p17), .out(data_mem_interface_1_p19),
    .sel(data_mem_interface_1_p18));

  // Notes on the sheet:
  //   F19
  //   Your Name
  //   Today's Date
  //   Decode
  //   Extend
  //   EX/Mem
  //   Mem/WB
endmodule
