// Logisim project pipelineRegisters.circ as structural Verilog: 12 circuits, main circuit PipeReg2PC
module PipeReg1 (
  input  [31:0] PC,
  input  [31:0] Instruction,
  input  Clock,
  input  Reset,
  output [31:0] PC_out,
  output [31:0] IR_out
);

  Register #(.width(32)) PC_Reg (.D(PC), .Q(PC_out), .clk(Clock), .clr(Reset));  // open: en
  Register #(.width(32)) IR (.D(Instruction), .Q(IR_out), .clk(Clock), .clr(Reset));  // open: en

  // Notes on the sheet:
  //   S19
endmodule

module PipeReg2PC (
  input  [31:0] PC_in,
  input  Clock,
  input  Reset,
  output [31:0] PC_out
);

  Register #(.width(32)) PC_reg (.D(PC_in), .Q(PC_out), .clk(Clock), .clr(Reset));  // open: en
endmodule

module PipeReg2DP (
  input  [31:0] A_Register,
  input  [31:0] B_Register,
  input  [31:0] Sign_Ext,
  input  Clock,
  input  Reset,
  output [31:0] A_Reg,
  output [31:0] B_Reg,
  output [31:0] Sign_Ext_2
);

  Register #(.width(32)) u_A_reg (.D(A_Register), .Q(A_Reg), .clk(Clock), .clr(Reset));  // open: en
  Register #(.width(32)) u_B_Reg (.D(B_Register), .Q(B_Reg), .clk(Clock), .clr(Reset));  // open: en
  Register #(.width(32)) Immediate_sign_extended (.D(Sign_Ext), .Q(Sign_Ext_2), .clk(Clock), .clr(Reset));  // open: en
endmodule

module PipeReg2ALUCtrRt (
  input  [3:0] ALU_ctrl,
  input  [4:0] Rt,
  input  Clock,
  input  Reset,
  output [3:0] ALU_ctrl_out,
  output [4:0] Rt_out
);

  Register #(.width(4)) ALU_Control (.D(ALU_ctrl), .Q(ALU_ctrl_out), .clk(Clock), .clr(Reset));  // open: en
  Register #(.width(5)) u_Rt (.D(Rt), .Q(Rt_out), .clk(Clock), .clr(Reset));  // open: en
endmodule

module PipeReg2Ctrl (
  input  Unconditional_Branch,
  input  Conditional_Branch,
  input  MemToReg,
  input  MemRead,
  input  MemWrite,
  input  ALUsrc,
  input  RegWrite,
  input  Clock,
  input  Reset,
  output Uncond_Branch_out,
  output Cond_Branch_out,
  output MemToReg_out,
  output MemRead_out,
  output MemWrite_2,
  output ALUsrc_out,
  output RegWrite_out
);

  Register #(.width(7)) PipelineReg2c (
    .D({RegWrite, ALUsrc, MemWrite, MemRead, MemToReg, Conditional_Branch, Unconditional_Branch}),
    .Q({RegWrite_out, ALUsrc_out, MemWrite_2, MemRead_out, MemToReg_out, Cond_Branch_out, Uncond_Branch_out}),
    .clk(Clock), .clr(Reset));  // open: en
endmodule

module PipeReg3ALURt (
  input  Zero,
  input  [31:0] Result,
  input  [31:0] B_reg,
  input  Clock,
  input  Reset,
  output Zero_2,
  output [31:0] Result_2,
  output [31:0] B_reg_2
);

  Register #(.width(1)) u_Zero (.D(Zero), .Q(Zero_2), .clk(Clock), .clr(Reset));  // open: en
  Register #(.width(32)) u_Result (.D(Result), .Q(Result_2), .clk(Clock), .clr(Reset));  // open: en
  Register #(.width(32)) u_B_reg (.D(B_reg), .Q(B_reg_2), .clk(Clock), .clr(Reset));  // open: en
endmodule

module PipeReg3RdRt (
  input  [4:0] Rd_Rt_in,
  input  Clock,
  input  Reset,
  output [4:0] Rd_Rt_out
);

  Register #(.width(5)) Rd_RT (.D(Rd_Rt_in), .Q(Rd_Rt_out), .clk(Clock), .clr(Reset));  // open: en
endmodule

module PipeReg3Address (
  input  [31:0] Rd_Rt_in,
  input  Clock,
  input  Reset,
  output [31:0] Rd_Rt_out
);

  Register #(.width(32)) Rd_RT (.D(Rd_Rt_in), .Q(Rd_Rt_out), .clk(Clock), .clr(Reset));  // open: en
endmodule

module PipeReg3Ctrl (
  input  Unconditional_Branch,
  input  Conditional_Branch,
  input  MemToReg,
  input  MemRead,
  input  MemWrite,
  input  RegWrite,
  input  Clock,
  input  Reset,
  output Uncond_Branch_out,
  output Cond_Branch_out,
  output MemToReg_out,
  output MemRead_out,
  output MemWrite_2,
  output RegWrite_out
);

  Register #(.width(6)) PipelineReg3c (
    .D({RegWrite, MemWrite, MemRead, MemToReg, Conditional_Branch, Unconditional_Branch}),
    .Q({RegWrite_out, MemWrite_2, MemRead_out, MemToReg_out, Cond_Branch_out, Uncond_Branch_out}),
    .clk(Clock), .clr(Reset));  // open: en
endmodule

module PipeReg4RdRt (
  input  [4:0] Rd_Rt_in,
  input  Clock,
  input  Reset,
  output [4:0] Rd_Rt_out
);

  Register #(.width(5)) Rd_RT (.D(Rd_Rt_in), .Q(Rd_Rt_out), .clk(Clock), .clr(Reset));  // open: en
endmodule

module PipeReg4DataFromMem (
  input  [31:0] A_Register,
  input  [31:0] B_Register,
  input  Clock,
  input  Reset,
  output [31:0] A_Reg,
  output [31:0] B_Reg
);

  Register #(.width(32)) u_A_reg (.D(A_Register), .Q(A_Reg), .clk(Clock), .clr(Reset));  // open: en
  Register #(.width(32)) u_B_Reg (.D(B_Register), .Q(B_Reg), .clk(Clock), .clr(Reset));  // open: en
endmodule

module PipeReg4 (
  input  Zero,
  input  Zero_2,
  input  Clock,
  input  Reset,
  output Zero_3,
  output Zero_4
);

  Register #(.width(1)) u_Zero (.D(Zero), .Q(Zero_3), .clk(Clock), .clr(Reset));  // open: en
  Register #(.width(1)) u_Zero_2 (.D(Zero_2), .Q(Zero_4), .clk(Clock), .clr(Reset));  // open: en
endmodule
